// Logisim project Logisim primer kola.circ as structural Verilog: 1 circuit, main circuit Primer kola
module Primer_kola (
  input  X1,
  input  X2,
  output Y1
);

  wire not_1_out, or_1_out, or_2_out;

  not not_1 (not_1_out, X2);
  or or_1 (or_1_out, X2, X1);
  or or_2 (or_2_out, not_1_out, X1);
  and and_1 (Y1, or_1_out, or_2_out);
endmodule
